// Logisim project Computer4Bit.circ as structural Verilog: 11 circuits, main circuit CPU
module CPU (
  input  ProgrammingMode
);

  wire alu_8_bit_1_carry_out, C_out, clock_1_out, comparator_1_eq, delay_1_out_2, delay_2_out_2,
       delay_3_out_2, demultiplexer_1_out0, demultiplexer_1_out1, demultiplexer_1_out2, demultiplexer_1_out5,
       demultiplexer_1_out6, demultiplexer_1_out7, demultiplexer_1_out8, demultiplexer_1_out11,
       demultiplexer_1_out12, nor_1_out, not_1_out, not_3_out, not_4_out, OP_CARRY_q, or_1_out, or_2_out,
       or_3_out, or_4_out, or_6_out, or_8_out, or_9_out, r_edge_detector_1_out_2, r_edge_detector_2_out_2,
       R_out, ssd_1_out_2, ssd_1_out_3, ssd_1_out_4, ssd_1_out_5, ssd_1_out_6, ssd_1_out_7, ssd_1_out_8,
       ssd_2_out_2, ssd_2_out_3, ssd_2_out_4, ssd_2_out_5, ssd_2_out_6, ssd_2_out_7, ssd_2_out_8,
       ssd_3_out_2, ssd_3_out_3, ssd_3_out_4, ssd_3_out_5, ssd_3_out_6, ssd_3_out_7, ssd_3_out_8,
       ssd_4_out_2, ssd_4_out_3, ssd_4_out_4, ssd_4_out_5, ssd_4_out_6, ssd_4_out_7, ssd_4_out_8,
       ssd_5_out_2, ssd_5_out_3, ssd_5_out_4, ssd_5_out_5, ssd_5_out_6, ssd_5_out_7, ssd_5_out_8,
       ssd_6_out_2, ssd_6_out_3, ssd_6_out_4, ssd_6_out_5, ssd_6_out_6, ssd_6_out_7, ssd_6_out_8,
       ssd_7_out_2, ssd_7_out_3, ssd_7_out_4, ssd_7_out_5, ssd_7_out_6, ssd_7_out_7, ssd_7_out_8,
       ssd_8_out_2, ssd_8_out_3, ssd_8_out_4, ssd_8_out_5, ssd_8_out_6, ssd_8_out_7, ssd_8_out_8,
       ssd_9_out_2, ssd_9_out_3, ssd_9_out_4, ssd_9_out_5, ssd_9_out_6, ssd_9_out_7, ssd_9_out_8,
       ssd_10_out_2, ssd_10_out_3, ssd_10_out_4, ssd_10_out_5, ssd_10_out_6, ssd_10_out_7, ssd_10_out_8,
       ssd_11_out_2, ssd_11_out_3, ssd_11_out_4, ssd_11_out_5, ssd_11_out_6, ssd_11_out_7, ssd_11_out_8,
       ssd_12_out_2, ssd_12_out_3, ssd_12_out_4, ssd_12_out_5, ssd_12_out_6, ssd_12_out_7, ssd_12_out_8,
       ssd_13_out_2, ssd_13_out_3, ssd_13_out_4, ssd_13_out_5, ssd_13_out_6, ssd_13_out_7, ssd_13_out_8,
       ssd_14_out_2, ssd_14_out_3, ssd_14_out_4, ssd_14_out_5, ssd_14_out_6, ssd_14_out_7, ssd_14_out_8;
  wire [1:0] bitfinder_1_index, or_10_out;
  wire [3:0] binarytodec8bit_1_out_2, binarytodec8bit_1_out_3, binarytodec8bit_1_out_4,
       binarytodec8bit_2_out_2, binarytodec8bit_2_out_3, binarytodec8bit_2_out_4, binarytodec8bit_3_out_2,
       binarytodec8bit_3_out_3, binarytodec8bit_3_out_4, binarytodec8bit_4_out_2, binarytodec8bit_4_out_3,
       binarytodec8bit_4_out_4, demultiplexer_1_out3, MEM_REG_q;
  wire [7:0] alu_8_bit_1_output_8_bit, and_1_out, and_2_out, CACHE_dout, IR_q, leftshift_1_out_4,
       multiplexer_1_out, multiplexer_2_out, multiplexer_3_out, multiplexer_5_out, or_7_out,
       prog_count_1_out_8bit, ram_1_dout, REG_A_q, REG_B_q;
  wire [7:7] demultiplexer_1_out9, demultiplexer_1_out10;
  wire [9:8] demultiplexer_1_out13;
  wire [17:0] MemAddr_sw8, multiplexer_4_out;

  Clock clock_1 (.out(clock_1_out));
  Button C (.out(C_out));
  or or_1 (or_1_out, clock_1_out, C_out);
  Comparator #(.width(4)) comparator_1 (.a(IR_q[7:4]), .b(4'b1111), .eq(comparator_1_eq));  // open: gt, lt
  Button R (.out(R_out));
  not not_1 (not_1_out, comparator_1_eq);
  R_Edge_Detector r_edge_detector_1 (.out_2(r_edge_detector_1_out_2), .in_1(or_1_out));
  DELAY delay_1 (.in_1(r_edge_detector_1_out_2), .out_2(delay_1_out_2));
  or or_2 (or_2_out, R_out, ProgrammingMode);
  R_Edge_Detector r_edge_detector_2 (.out_2(r_edge_detector_2_out_2), .in_1(delay_2_out_2));
  DELAY delay_2 (.in_1(or_9_out), .out_2(delay_2_out_2));
  DELAY delay_3 (.in_1(or_1_out), .out_2(delay_3_out_2));
  Demultiplexer #(.select(4), .enable("false")) demultiplexer_1 (
    .out0(demultiplexer_1_out0), .out1(demultiplexer_1_out1), .out2(demultiplexer_1_out2),
    .out3(demultiplexer_1_out3[0]), .out4(demultiplexer_1_out3[1]), .out5(demultiplexer_1_out5),
    .out6(demultiplexer_1_out6), .out7(demultiplexer_1_out7), .out8(demultiplexer_1_out8),
    .out9(demultiplexer_1_out9[7]), .out10(demultiplexer_1_out10[7]), .out11(demultiplexer_1_out11),
    .out12(demultiplexer_1_out12), .out13(demultiplexer_1_out13[8]), .out14(demultiplexer_1_out3[3]),
    .in(delay_3_out_2), .sel(IR_q[7:4]));  // open: out15
  PROG_COUNT prog_count_1 (
    .Out_8bit(prog_count_1_out_8bit), .Clk(delay_1_out_2), .Enable(not_1_out), .Reset(or_2_out),
    .IN_8_BIT(or_7_out), .SET(r_edge_detector_2_out_2));
  or or_3 (or_3_out, demultiplexer_1_out3[0], demultiplexer_1_out3[1], demultiplexer_1_out5, demultiplexer_1_out6, demultiplexer_1_out11, demultiplexer_1_out12, demultiplexer_1_out3[3]);
  or or_4 (or_4_out, demultiplexer_1_out9[7], demultiplexer_1_out2, demultiplexer_1_out1, demultiplexer_1_out10[7]);
  or or_5 (demultiplexer_1_out3[2], demultiplexer_1_out5, demultiplexer_1_out6, demultiplexer_1_out11, demultiplexer_1_out12);
  Multiplexer #(.width(8), .enable("false")) multiplexer_1 (
    .in0(prog_count_1_out_8bit), .in1(REG_B_q), .out(multiplexer_1_out), .sel(demultiplexer_1_out13[8]));
  not not_2 (demultiplexer_1_out13[9], demultiplexer_1_out13[8]);
  DipSwitch MemAddr (
    .sw1(MemAddr_sw8[7]), .sw2(MemAddr_sw8[6]), .sw3(MemAddr_sw8[5]), .sw4(MemAddr_sw8[4]),
    .sw5(MemAddr_sw8[3]), .sw6(MemAddr_sw8[2]), .sw7(MemAddr_sw8[1]), .sw8(MemAddr_sw8[0]));
  DipSwitch Value (
    .sw1(MemAddr_sw8[17]), .sw2(MemAddr_sw8[16]), .sw3(MemAddr_sw8[15]), .sw4(MemAddr_sw8[14]),
    .sw5(MemAddr_sw8[13]), .sw6(MemAddr_sw8[12]), .sw7(MemAddr_sw8[11]), .sw8(MemAddr_sw8[10]));
  Multiplexer #(.width(8), .enable("false")) multiplexer_2 (
    .in0(prog_count_1_out_8bit), .in1(CACHE_dout), .out(multiplexer_2_out), .sel(not_3_out));
  nor nor_1 (nor_1_out, demultiplexer_1_out7, demultiplexer_1_out8);
  or or_6 (or_6_out, demultiplexer_1_out1, demultiplexer_1_out7);
  Register #(.width(4), .trigger("high")) MEM_REG (
    .D(IR_q[3:0]), .en(demultiplexer_1_out0), .clk(demultiplexer_1_out0), .Q(MEM_REG_q), .clr(or_2_out));
  Button button_1 (.out(MemAddr_sw8[8]));
  assign and_1_out = multiplexer_2_out & {8{demultiplexer_1_out10[7]}};  // AND_Gate and_1, 8 bits wide
  assign or_7_out = and_1_out | and_2_out;  // OR_Gate or_7, 8 bits wide
  assign and_2_out = CACHE_dout & {8{demultiplexer_1_out9[7]}};  // AND_Gate and_2, 8 bits wide
  not not_3 (not_3_out, OP_CARRY_q);
  Multiplexer #(.width(8), .enable("false")) multiplexer_3 (
    .in0({4'b0000, IR_q[3:0]}), .in1(CACHE_dout), .out(multiplexer_3_out), .sel(nor_1_out));
  or or_8 (or_8_out, demultiplexer_1_out2, demultiplexer_1_out8);
  BitFinder #(.width(4)) bitfinder_1 (.in(demultiplexer_1_out3), .index(bitfinder_1_index));  // open: found
  Multiplexer #(.width(18), .enable("false")) multiplexer_4 (
    .in0({REG_A_q, demultiplexer_1_out13, multiplexer_1_out}),
    .in1({MemAddr_sw8[17:10], 1'b0, MemAddr_sw8[8:0]}), .out(multiplexer_4_out), .sel(ProgrammingMode));
  RAM #(.trigger("high"), .databus("bibus")) ram_1 (
    .addr(multiplexer_4_out[7:0]), .we(multiplexer_4_out[8]), .oe(multiplexer_4_out[9]),
    .din(multiplexer_4_out[17:10]), .dout(ram_1_dout));
  or or_9 (or_9_out, demultiplexer_1_out10[7], demultiplexer_1_out9[7]);
  Register #(.trigger("high")) REG_A (
    .D(multiplexer_3_out), .en(or_6_out), .clk(or_6_out), .Q(REG_A_q), .clr(or_2_out));
  Register #(.trigger("high")) REG_B (
    .D(multiplexer_3_out), .en(or_8_out), .clk(or_8_out), .Q(REG_B_q), .clr(or_2_out));
  or or_10 (or_10_out[0], demultiplexer_1_out6, demultiplexer_1_out12);
  or or_11 (or_10_out[1], demultiplexer_1_out11, demultiplexer_1_out12);
  not not_4 (not_4_out, comparator_1_eq);
  RAM #(.trigger("high"), .databus("bibus")) CACHE (
    .addr({MEM_REG_q, IR_q[3:0]}), .we(or_3_out), .oe(or_4_out), .din(multiplexer_5_out), .dout(CACHE_dout));
  Multiplexer #(.select(2), .width(8), .disabled("Z")) multiplexer_5 (
    .in0(REG_A_q), .in1(REG_B_q), .in2(alu_8_bit_1_output_8_bit), .in3(leftshift_1_out_4),
    .out(multiplexer_5_out), .sel(bitfinder_1_index), .en(not_4_out));
  ALU_8_BIT alu_8_bit_1 (
    .OUTPUT_8_BIT(alu_8_bit_1_output_8_bit), .INPUT_8_BIT_1(REG_A_q), .INPUT_8_BIT_2(REG_B_q),
    .CARRY_OUT(alu_8_bit_1_carry_out), .MODE(or_10_out));
  LEFTSHIFT leftshift_1 (.out_4(leftshift_1_out_4), .SHIFT_VAL(4'b0100), .IN_8_BIT(REG_A_q), .CARRY_IN(REG_B_q));
  Register IR (.D(ram_1_dout), .en(1'b1), .clk(r_edge_detector_1_out_2), .Q(IR_q), .clr(or_2_out));
  Register #(.width(1), .trigger("high")) OP_CARRY (
    .D(alu_8_bit_1_carry_out), .en(demultiplexer_1_out3[2]), .clk(demultiplexer_1_out3[2]), .Q(OP_CARRY_q),
    .clr(or_2_out));
  _7_Segment_Display u_7_segment_display_1 (
    .g(ssd_1_out_2), .f(ssd_1_out_3), .a(ssd_1_out_4), .b(ssd_1_out_5), .e(ssd_1_out_6), .d(ssd_1_out_7),
    .c(ssd_1_out_8));  // open: dp
  SSD ssd_1 (
    .out_7(ssd_1_out_7), .out_6(ssd_1_out_6), .out_5(ssd_1_out_5), .out_4(ssd_1_out_4), .out_3(ssd_1_out_3),
    .out_2(ssd_1_out_2), .in_1(IR_q[7:4]), .out_8(ssd_1_out_8));
  BinaryToDec8bit binarytodec8bit_1 (
    .out_4(binarytodec8bit_1_out_4), .out_3(binarytodec8bit_1_out_3), .out_2(binarytodec8bit_1_out_2),
    .in_1(REG_A_q));
  BinaryToDec8bit binarytodec8bit_2 (
    .out_4(binarytodec8bit_2_out_4), .out_3(binarytodec8bit_2_out_3), .out_2(binarytodec8bit_2_out_2),
    .in_1(REG_B_q));
  BinaryToDec8bit binarytodec8bit_3 (
    .out_4(binarytodec8bit_3_out_4), .out_3(binarytodec8bit_3_out_3), .out_2(binarytodec8bit_3_out_2),
    .in_1({MEM_REG_q, IR_q[3:0]}));
  BinaryToDec8bit binarytodec8bit_4 (
    .out_4(binarytodec8bit_4_out_4), .out_3(binarytodec8bit_4_out_3), .out_2(binarytodec8bit_4_out_2),
    .in_1(CACHE_dout));
  _7_Segment_Display u_7_segment_display_2 (
    .g(ssd_2_out_2), .f(ssd_2_out_3), .a(ssd_2_out_4), .b(ssd_2_out_5), .e(ssd_2_out_6), .d(ssd_2_out_7),
    .c(ssd_2_out_8));  // open: dp
  SSD ssd_2 (
    .out_7(ssd_2_out_7), .out_6(ssd_2_out_6), .out_5(ssd_2_out_5), .out_4(ssd_2_out_4), .out_3(ssd_2_out_3),
    .out_2(ssd_2_out_2), .in_1(IR_q[3:0]), .out_8(ssd_2_out_8));
  _7_Segment_Display u_7_segment_display_3 (
    .g(ssd_3_out_2), .f(ssd_3_out_3), .a(ssd_3_out_4), .b(ssd_3_out_5), .e(ssd_3_out_6), .d(ssd_3_out_7),
    .c(ssd_3_out_8));  // open: dp
  SSD ssd_3 (
    .out_7(ssd_3_out_7), .out_6(ssd_3_out_6), .out_5(ssd_3_out_5), .out_4(ssd_3_out_4), .out_3(ssd_3_out_3),
    .out_2(ssd_3_out_2), .in_1(binarytodec8bit_3_out_2), .out_8(ssd_3_out_8));
  _7_Segment_Display u_7_segment_display_4 (
    .g(ssd_4_out_2), .f(ssd_4_out_3), .a(ssd_4_out_4), .b(ssd_4_out_5), .e(ssd_4_out_6), .d(ssd_4_out_7),
    .c(ssd_4_out_8));  // open: dp
  SSD ssd_4 (
    .out_7(ssd_4_out_7), .out_6(ssd_4_out_6), .out_5(ssd_4_out_5), .out_4(ssd_4_out_4), .out_3(ssd_4_out_3),
    .out_2(ssd_4_out_2), .in_1(binarytodec8bit_4_out_2), .out_8(ssd_4_out_8));
  _7_Segment_Display u_7_segment_display_5 (
    .g(ssd_6_out_2), .f(ssd_6_out_3), .a(ssd_6_out_4), .b(ssd_6_out_5), .e(ssd_6_out_6), .d(ssd_6_out_7),
    .c(ssd_6_out_8));  // open: dp
  _7_Segment_Display u_7_segment_display_6 (
    .g(ssd_5_out_2), .f(ssd_5_out_3), .a(ssd_5_out_4), .b(ssd_5_out_5), .e(ssd_5_out_6), .d(ssd_5_out_7),
    .c(ssd_5_out_8));  // open: dp
  SSD ssd_5 (
    .out_7(ssd_5_out_7), .out_6(ssd_5_out_6), .out_5(ssd_5_out_5), .out_4(ssd_5_out_4), .out_3(ssd_5_out_3),
    .out_2(ssd_5_out_2), .in_1(binarytodec8bit_1_out_2), .out_8(ssd_5_out_8));
  SSD ssd_6 (
    .out_7(ssd_6_out_7), .out_6(ssd_6_out_6), .out_5(ssd_6_out_5), .out_4(ssd_6_out_4), .out_3(ssd_6_out_3),
    .out_2(ssd_6_out_2), .in_1(binarytodec8bit_1_out_3), .out_8(ssd_6_out_8));
  _7_Segment_Display u_7_segment_display_7 (
    .g(ssd_8_out_2), .f(ssd_8_out_3), .a(ssd_8_out_4), .b(ssd_8_out_5), .e(ssd_8_out_6), .d(ssd_8_out_7),
    .c(ssd_8_out_8));  // open: dp
  _7_Segment_Display u_7_segment_display_8 (
    .g(ssd_7_out_2), .f(ssd_7_out_3), .a(ssd_7_out_4), .b(ssd_7_out_5), .e(ssd_7_out_6), .d(ssd_7_out_7),
    .c(ssd_7_out_8));  // open: dp
  SSD ssd_7 (
    .out_7(ssd_7_out_7), .out_6(ssd_7_out_6), .out_5(ssd_7_out_5), .out_4(ssd_7_out_4), .out_3(ssd_7_out_3),
    .out_2(ssd_7_out_2), .in_1(binarytodec8bit_2_out_2), .out_8(ssd_7_out_8));
  SSD ssd_8 (
    .out_7(ssd_8_out_7), .out_6(ssd_8_out_6), .out_5(ssd_8_out_5), .out_4(ssd_8_out_4), .out_3(ssd_8_out_3),
    .out_2(ssd_8_out_2), .in_1(binarytodec8bit_2_out_3), .out_8(ssd_8_out_8));
  _7_Segment_Display u_7_segment_display_9 (
    .g(ssd_9_out_2), .f(ssd_9_out_3), .a(ssd_9_out_4), .b(ssd_9_out_5), .e(ssd_9_out_6), .d(ssd_9_out_7),
    .c(ssd_9_out_8));  // open: dp
  SSD ssd_9 (
    .out_7(ssd_9_out_7), .out_6(ssd_9_out_6), .out_5(ssd_9_out_5), .out_4(ssd_9_out_4), .out_3(ssd_9_out_3),
    .out_2(ssd_9_out_2), .in_1(binarytodec8bit_3_out_3), .out_8(ssd_9_out_8));
  _7_Segment_Display u_7_segment_display_10 (
    .g(ssd_10_out_2), .f(ssd_10_out_3), .a(ssd_10_out_4), .b(ssd_10_out_5), .e(ssd_10_out_6),
    .d(ssd_10_out_7), .c(ssd_10_out_8));  // open: dp
  SSD ssd_10 (
    .out_7(ssd_10_out_7), .out_6(ssd_10_out_6), .out_5(ssd_10_out_5), .out_4(ssd_10_out_4),
    .out_3(ssd_10_out_3), .out_2(ssd_10_out_2), .in_1(binarytodec8bit_4_out_3), .out_8(ssd_10_out_8));
  _7_Segment_Display u_7_segment_display_11 (
    .g(ssd_11_out_2), .f(ssd_11_out_3), .a(ssd_11_out_4), .b(ssd_11_out_5), .e(ssd_11_out_6),
    .d(ssd_11_out_7), .c(ssd_11_out_8));  // open: dp
  SSD ssd_11 (
    .out_7(ssd_11_out_7), .out_6(ssd_11_out_6), .out_5(ssd_11_out_5), .out_4(ssd_11_out_4),
    .out_3(ssd_11_out_3), .out_2(ssd_11_out_2), .in_1(binarytodec8bit_1_out_4), .out_8(ssd_11_out_8));
  _7_Segment_Display u_7_segment_display_12 (
    .g(ssd_12_out_2), .f(ssd_12_out_3), .a(ssd_12_out_4), .b(ssd_12_out_5), .e(ssd_12_out_6),
    .d(ssd_12_out_7), .c(ssd_12_out_8));  // open: dp
  SSD ssd_12 (
    .out_7(ssd_12_out_7), .out_6(ssd_12_out_6), .out_5(ssd_12_out_5), .out_4(ssd_12_out_4),
    .out_3(ssd_12_out_3), .out_2(ssd_12_out_2), .in_1(binarytodec8bit_2_out_4), .out_8(ssd_12_out_8));
  _7_Segment_Display u_7_segment_display_13 (
    .g(ssd_13_out_2), .f(ssd_13_out_3), .a(ssd_13_out_4), .b(ssd_13_out_5), .e(ssd_13_out_6),
    .d(ssd_13_out_7), .c(ssd_13_out_8));  // open: dp
  SSD ssd_13 (
    .out_7(ssd_13_out_7), .out_6(ssd_13_out_6), .out_5(ssd_13_out_5), .out_4(ssd_13_out_4),
    .out_3(ssd_13_out_3), .out_2(ssd_13_out_2), .in_1(binarytodec8bit_3_out_4), .out_8(ssd_13_out_8));
  _7_Segment_Display u_7_segment_display_14 (
    .g(ssd_14_out_2), .f(ssd_14_out_3), .a(ssd_14_out_4), .b(ssd_14_out_5), .e(ssd_14_out_6),
    .d(ssd_14_out_7), .c(ssd_14_out_8));  // open: dp
  SSD ssd_14 (
    .out_7(ssd_14_out_7), .out_6(ssd_14_out_6), .out_5(ssd_14_out_5), .out_4(ssd_14_out_4),
    .out_3(ssd_14_out_3), .out_2(ssd_14_out_2), .in_1(binarytodec8bit_4_out_4), .out_8(ssd_14_out_8));
endmodule

module ALU_8_BIT (
  input  [7:0] INPUT_8_BIT_1,
  input  [7:0] INPUT_8_BIT_2,
  input  [1:0] MODE,
  output [7:0] OUTPUT_8_BIT,
  output CARRY_OUT
);

  wire adder_1_cout, comparator_1_gt, comparator_1_lt, comparator_2_gt, comparator_2_lt, or_1_out, or_2_out,
       subtractor_1_bout;
  wire [7:0] adder_1_out, divider_1_out, divider_1_rem, multiplier_1_cout, multiplier_1_out, subtractor_1_out;

  Multiplexer #(.select(2), .enable("false")) multiplexer_1 (
    .in0(adder_1_cout), .in1(subtractor_1_bout), .in2(or_2_out), .in3(or_1_out), .out(CARRY_OUT), .sel(MODE));
  Adder adder_1 (.a(INPUT_8_BIT_1), .b(INPUT_8_BIT_2), .out(adder_1_out), .cin(1'b0), .cout(adder_1_cout));
  Subtractor subtractor_1 (
    .a(INPUT_8_BIT_1), .b(INPUT_8_BIT_2), .out(subtractor_1_out), .bin(1'b0), .bout(subtractor_1_bout));
  Multiplier multiplier_1 (
    .a(INPUT_8_BIT_1), .b(INPUT_8_BIT_2), .out(multiplier_1_out), .cout(multiplier_1_cout));  // open: cin
  Divider divider_1 (.a(INPUT_8_BIT_1), .b(INPUT_8_BIT_2), .out(divider_1_out), .rem(divider_1_rem));  // open: upper
  Comparator comparator_1 (.a(divider_1_rem), .b({8{1'b0}}), .gt(comparator_1_gt), .lt(comparator_1_lt));  // open: eq
  or or_1 (or_1_out, comparator_1_gt, comparator_1_lt);
  Comparator comparator_2 (
    .a(multiplier_1_cout), .b({8{1'b0}}), .gt(comparator_2_gt), .lt(comparator_2_lt));  // open: eq
  or or_2 (or_2_out, comparator_2_gt, comparator_2_lt);
  Multiplexer #(.select(2), .width(8), .enable("false")) multiplexer_2 (
    .in0(adder_1_out), .in1(subtractor_1_out), .in2(multiplier_1_out), .in3(divider_1_out),
    .out(OUTPUT_8_BIT), .sel(MODE));

  // Notes on the sheet:
  //   ALU that can compute the sum or difference between two values
endmodule

module PROG_COUNT (
  input  [7:0] IN_8_BIT,
  input  SET,
  input  Enable,
  input  Reset,
  input  Clk,
  output [7:0] Out_8bit
);

  wire and_1_out, and_2_out, and_3_out, and_4_out, and_5_out, and_6_out, and_7_out, and_8_out, and_9_out,
       and_10_out, and_11_out, and_12_out, and_13_out, and_14_out, and_15_out, c_edge_detector_1_out_2,
       c_edge_detector_1_out_3, or_1_out;

  C_Edge_Detector c_edge_detector_1 (.out_3(c_edge_detector_1_out_3), .out_2(c_edge_detector_1_out_2), .in_1(SET));
  or or_1 (or_1_out, c_edge_detector_1_out_2, Reset);
  and and_1 (and_1_out, c_edge_detector_1_out_3, IN_8_BIT[0]);
  T_Flip_Flop t_ff_1 (.T(Enable), .clk(Clk), .Q(Out_8bit[0]), .reset(or_1_out), .preset(and_1_out));  // open: Qn
  and and_2 (and_2_out, c_edge_detector_1_out_3, IN_8_BIT[1]);
  T_Flip_Flop t_ff_2 (.T(and_3_out), .clk(Clk), .Q(Out_8bit[1]), .reset(or_1_out), .preset(and_2_out));  // open: Qn
  and and_3 (and_3_out, Enable, Out_8bit[0]);
  T_Flip_Flop t_ff_3 (.T(and_4_out), .clk(Clk), .Q(Out_8bit[2]), .reset(or_1_out), .preset(and_5_out));  // open: Qn
  and and_4 (and_4_out, and_3_out, Out_8bit[1]);
  and and_5 (and_5_out, c_edge_detector_1_out_3, IN_8_BIT[2]);
  T_Flip_Flop t_ff_4 (.T(and_6_out), .clk(Clk), .Q(Out_8bit[3]), .reset(or_1_out), .preset(and_7_out));  // open: Qn
  and and_6 (and_6_out, and_4_out, Out_8bit[2]);
  and and_7 (and_7_out, c_edge_detector_1_out_3, IN_8_BIT[3]);
  and and_8 (and_8_out, and_6_out, Out_8bit[3]);
  and and_9 (and_9_out, c_edge_detector_1_out_3, IN_8_BIT[4]);
  T_Flip_Flop t_ff_5 (.T(and_8_out), .clk(Clk), .Q(Out_8bit[4]), .reset(or_1_out), .preset(and_9_out));  // open: Qn
  and and_10 (and_10_out, c_edge_detector_1_out_3, IN_8_BIT[5]);
  T_Flip_Flop t_ff_6 (.T(and_11_out), .clk(Clk), .Q(Out_8bit[5]), .reset(or_1_out), .preset(and_10_out));  // open: Qn
  and and_11 (and_11_out, and_8_out, Out_8bit[4]);
  and and_12 (and_12_out, c_edge_detector_1_out_3, IN_8_BIT[6]);
  T_Flip_Flop t_ff_7 (.T(and_13_out), .clk(Clk), .Q(Out_8bit[6]), .reset(or_1_out), .preset(and_12_out));  // open: Qn
  and and_13 (and_13_out, and_11_out, Out_8bit[5]);
  and and_14 (and_14_out, c_edge_detector_1_out_3, IN_8_BIT[7]);
  T_Flip_Flop t_ff_8 (.T(and_15_out), .clk(Clk), .Q(Out_8bit[7]), .reset(or_1_out), .preset(and_14_out));  // open: Qn
  and and_15 (and_15_out, and_13_out, Out_8bit[6]);

  // Notes on the sheet:
  //   Enable: pull=up
  //   Reset: pull=down
endmodule

module LEFTSHIFT (
  input  [7:0] IN_8_BIT,
  input  [3:0] SHIFT_VAL,
  input  [7:0] CARRY_IN,
  output [7:0] out_4
);

  wire [7:0] decoder_1_out0, multiplier_1_out;

  Decoder #(.select(4), .enable("false")) decoder_1 (
    .out0(decoder_1_out0[0]), .out1(decoder_1_out0[1]), .out2(decoder_1_out0[2]), .out3(decoder_1_out0[3]),
    .out4(decoder_1_out0[4]), .out5(decoder_1_out0[5]), .out6(decoder_1_out0[6]), .out7(decoder_1_out0[7]),
    .sel(SHIFT_VAL));  // open: out8, out9, out10, out11, out12, out13, out14, out15
  Multiplier multiplier_1 (.a(IN_8_BIT), .b(decoder_1_out0), .out(multiplier_1_out));  // open: cin, cout
  Adder adder_1 (.a(multiplier_1_out), .b(CARRY_IN), .out(out_4));  // open: cin, cout
endmodule

module DELAY (
  input  in_1,
  output out_2
);

  wire not_1_out, not_2_out, not_3_out, not_4_out, not_5_out, not_6_out, not_7_out, not_8_out, not_9_out,
       not_10_out, not_11_out, not_12_out, not_13_out, not_14_out, not_15_out, not_16_out, not_17_out,
       not_18_out, not_19_out, not_20_out, not_21_out, not_22_out, not_23_out, not_24_out, not_25_out,
       not_26_out, not_27_out, not_28_out, not_29_out, not_30_out, not_31_out, not_32_out, not_33_out,
       not_34_out, not_35_out, not_36_out, not_37_out, not_38_out, not_39_out, not_40_out, not_41_out,
       not_42_out, not_43_out, not_44_out, not_45_out, not_46_out, not_47_out, not_48_out, not_49_out,
       not_50_out, not_51_out, not_52_out, not_53_out, not_54_out, not_55_out, not_56_out, not_57_out,
       not_58_out, not_59_out, not_60_out, not_61_out, not_62_out, not_63_out, not_64_out, not_65_out,
       not_66_out, not_67_out, not_68_out, not_69_out, not_70_out, not_71_out, not_72_out, not_73_out,
       not_74_out, not_75_out, not_76_out, not_77_out, not_78_out, not_79_out, not_80_out, not_81_out,
       not_82_out, not_83_out, not_84_out, not_85_out, not_86_out, not_87_out, not_88_out, not_89_out,
       not_90_out, not_91_out, not_92_out, not_93_out, not_94_out, not_95_out, not_96_out, not_97_out,
       not_98_out, not_99_out, not_100_out, not_101_out, not_102_out, not_103_out, not_104_out, not_105_out,
       not_106_out, not_107_out, not_108_out, not_109_out, not_110_out, not_111_out;

  not not_1 (not_1_out, in_1);
  not not_2 (not_2_out, not_94_out);
  not not_3 (not_3_out, not_96_out);
  not not_4 (not_4_out, not_100_out);
  not not_5 (not_5_out, not_103_out);
  not not_6 (not_6_out, not_104_out);
  not not_7 (not_7_out, not_109_out);
  not not_8 (not_8_out, not_1_out);
  not not_9 (not_9_out, not_10_out);
  not not_10 (not_10_out, not_8_out);
  not not_11 (not_11_out, not_9_out);
  not not_12 (not_12_out, not_2_out);
  not not_13 (not_13_out, not_14_out);
  not not_14 (not_14_out, not_15_out);
  not not_15 (not_15_out, not_12_out);
  not not_16 (not_16_out, not_3_out);
  not not_17 (not_17_out, not_19_out);
  not not_18 (not_18_out, not_16_out);
  not not_19 (not_19_out, not_18_out);
  not not_20 (not_20_out, not_23_out);
  not not_21 (not_21_out, not_4_out);
  not not_22 (not_22_out, not_20_out);
  not not_23 (not_23_out, not_21_out);
  not not_24 (not_24_out, not_27_out);
  not not_25 (not_25_out, not_26_out);
  not not_26 (not_26_out, not_5_out);
  not not_27 (not_27_out, not_25_out);
  not not_28 (not_28_out, not_30_out);
  not not_29 (not_29_out, not_31_out);
  not not_30 (not_30_out, not_6_out);
  not not_31 (not_31_out, not_28_out);
  not not_32 (not_32_out, not_33_out);
  not not_33 (not_33_out, not_34_out);
  not not_34 (not_34_out, not_7_out);
  not not_35 (not_35_out, not_32_out);
  not not_36 (not_36_out, not_38_out);
  not not_37 (not_37_out, not_11_out);
  not not_38 (not_38_out, not_37_out);
  not not_39 (not_39_out, not_36_out);
  not not_40 (not_40_out, not_43_out);
  not not_41 (not_41_out, not_42_out);
  not not_42 (not_42_out, not_40_out);
  not not_43 (not_43_out, not_13_out);
  not not_44 (not_44_out, not_46_out);
  not not_45 (not_45_out, not_17_out);
  not not_46 (not_46_out, not_47_out);
  not not_47 (not_47_out, not_45_out);
  not not_48 (not_48_out, not_50_out);
  not not_49 (not_49_out, not_22_out);
  not not_50 (not_50_out, not_49_out);
  not not_51 (not_51_out, not_48_out);
  not not_52 (not_52_out, not_55_out);
  not not_53 (not_53_out, not_24_out);
  not not_54 (not_54_out, not_53_out);
  not not_55 (not_55_out, not_54_out);
  not not_56 (not_56_out, not_57_out);
  not not_57 (not_57_out, not_58_out);
  not not_58 (not_58_out, not_29_out);
  not not_59 (not_59_out, not_56_out);
  not not_60 (not_60_out, not_63_out);
  not not_61 (not_61_out, not_35_out);
  not not_62 (not_62_out, not_60_out);
  not not_63 (not_63_out, not_61_out);
  not not_64 (not_64_out, not_66_out);
  not not_65 (not_65_out, not_67_out);
  not not_66 (not_66_out, not_65_out);
  not not_67 (not_67_out, not_39_out);
  not not_68 (not_68_out, not_71_out);
  not not_69 (not_69_out, not_70_out);
  not not_70 (not_70_out, not_68_out);
  not not_71 (not_71_out, not_41_out);
  not not_72 (not_72_out, not_74_out);
  not not_73 (not_73_out, not_75_out);
  not not_74 (not_74_out, not_73_out);
  not not_75 (not_75_out, not_44_out);
  not not_76 (not_76_out, not_79_out);
  not not_77 (not_77_out, not_51_out);
  not not_78 (not_78_out, not_76_out);
  not not_79 (not_79_out, not_77_out);
  not not_80 (not_80_out, not_82_out);
  not not_81 (not_81_out, not_80_out);
  not not_82 (not_82_out, not_83_out);
  not not_83 (not_83_out, not_52_out);
  not not_84 (not_84_out, not_85_out);
  not not_85 (not_85_out, not_86_out);
  not not_86 (not_86_out, not_59_out);
  not not_87 (not_87_out, not_84_out);
  not not_88 (not_88_out, not_90_out);
  not not_89 (not_89_out, not_88_out);
  not not_90 (not_90_out, not_91_out);
  not not_91 (not_91_out, not_62_out);
  not not_92 (not_92_out, not_93_out);
  not not_93 (not_93_out, not_64_out);
  not not_94 (not_94_out, not_92_out);
  not not_95 (not_95_out, not_69_out);
  not not_96 (not_96_out, not_97_out);
  not not_97 (not_97_out, not_95_out);
  not not_98 (not_98_out, not_99_out);
  not not_99 (not_99_out, not_72_out);
  not not_100 (not_100_out, not_98_out);
  not not_101 (not_101_out, not_78_out);
  not not_102 (not_102_out, not_101_out);
  not not_103 (not_103_out, not_102_out);
  not not_104 (not_104_out, not_106_out);
  not not_105 (not_105_out, not_81_out);
  not not_106 (not_106_out, not_105_out);
  not not_107 (not_107_out, not_87_out);
  not not_108 (not_108_out, not_107_out);
  not not_109 (not_109_out, not_108_out);
  not not_110 (not_110_out, not_89_out);
  not not_111 (not_111_out, not_110_out);
  not not_112 (out_2, not_111_out);
endmodule

module C_Edge_Detector (
  input  in_1,
  output out_2,
  output out_3
);

  wire not_1_out, not_2_out, not_3_out;

  not not_1 (not_1_out, in_1);
  and and_1 (out_2, in_1, not_2_out);
  not not_2 (not_2_out, in_1);
  and and_2 (out_3, not_1_out, not_3_out);
  not not_3 (not_3_out, not_1_out);
endmodule

module R_Edge_Detector (
  input  in_1,
  output out_2
);

  wire not_1_out;

  and and_1 (out_2, in_1, not_1_out);
  not not_1 (not_1_out, in_1);
endmodule

module F_Edge_Detector (
  input  in_1,
  output out_2
);

  wire not_1_out, not_2_out;

  not not_1 (not_1_out, in_1);
  and and_1 (out_2, not_1_out, not_2_out);
  not not_2 (not_2_out, not_1_out);
endmodule

module B_Edge_Detector (
  input  in_1,
  output out_2
);

  wire and_1_out, and_2_out, not_1_out, not_2_out, not_3_out;

  not not_1 (not_1_out, in_1);
  and and_1 (and_1_out, in_1, not_2_out);
  not not_2 (not_2_out, in_1);
  and and_2 (and_2_out, not_1_out, not_3_out);
  not not_3 (not_3_out, not_1_out);
  or or_1 (out_2, and_1_out, and_2_out);
endmodule

module BinaryToDec8bit (
  input  [7:0] in_1,
  output [3:0] out_2,
  output [3:0] out_3,
  output [3:0] out_4
);

  wire [7:0] divider_1_out;
  wire [7:4] divider_1_rem, divider_2_out, divider_2_rem;

  Divider divider_1 (.a(in_1), .b(8'ha), .out(divider_1_out), .rem({divider_1_rem, out_4}));  // open: upper
  Divider divider_2 (
    .a(divider_1_out), .b(8'ha), .out({divider_2_out, out_2}), .rem({divider_2_rem, out_3}));  // open: upper
endmodule

module SSD (
  input  [3:0] in_1,
  output out_2,
  output out_3,
  output out_4,
  output out_5,
  output out_6,
  output out_7,
  output out_8
);

  wire decoder_1_out0, decoder_1_out1, decoder_1_out2, decoder_1_out3, decoder_1_out4, decoder_1_out5,
       decoder_1_out6, decoder_1_out7, decoder_1_out9, decoder_1_out10, decoder_1_out11, decoder_1_out12,
       decoder_1_out13, decoder_1_out14, decoder_1_out15;

  Decoder #(.select(4)) decoder_1 (
    .out0(decoder_1_out0), .out1(decoder_1_out1), .out2(decoder_1_out2), .out3(decoder_1_out3),
    .out4(decoder_1_out4), .out5(decoder_1_out5), .out6(decoder_1_out6), .out7(decoder_1_out7),
    .out9(decoder_1_out9), .out10(decoder_1_out10), .out11(decoder_1_out11), .out12(decoder_1_out12),
    .out13(decoder_1_out13), .out14(decoder_1_out14), .out15(decoder_1_out15), .sel(in_1));  // open: out8, en
  and and_1 (out_2, ~decoder_1_out0, ~decoder_1_out1, ~decoder_1_out7, ~decoder_1_out12);  // AND_Gate
  and and_2 (out_3, ~decoder_1_out1, ~decoder_1_out2, ~decoder_1_out3, ~decoder_1_out7, ~decoder_1_out13);  // AND_Gate
  and and_3 (out_4, ~decoder_1_out1, ~decoder_1_out4, ~decoder_1_out11, ~decoder_1_out13);  // AND_Gate
  and and_4 (out_5, ~decoder_1_out5, ~decoder_1_out6, ~decoder_1_out11, ~decoder_1_out12, ~decoder_1_out14, ~decoder_1_out15);  // AND_Gate
  and and_5 (out_6, ~decoder_1_out1, ~decoder_1_out3, ~decoder_1_out4, ~decoder_1_out5, ~decoder_1_out7, ~decoder_1_out9);  // AND_Gate
  and and_6 (out_7, ~decoder_1_out1, ~decoder_1_out4, ~decoder_1_out7, ~decoder_1_out9, ~decoder_1_out10, ~decoder_1_out15);  // AND_Gate
  and and_7 (out_8, ~decoder_1_out2, ~decoder_1_out12, ~decoder_1_out14, ~decoder_1_out15);  // AND_Gate
endmodule
